# Fritzing sketch esquema (saved by Fritzing 0.9.3b)
breadboards: 1

parts:
  Nano1 = Arduino Nano v2.3
  DHT1 = DHT22 Humidity and Temperature Sensor
  RF_433_MHz_(Transmissor)1 = RF 433 MHz (Receptor)
  R1 = 10K Ω Resistor [package=THT]

nets:
  GND: Nano1.GND, DHT1.GND, RF_433_MHz_(Transmissor)1.DATA_2
  N1: Nano1.D2, DHT1.DATA, R1.Pin_1
  N2: Nano1.D12, RF_433_MHz_(Transmissor)1.VCC
  +5V: Nano1.+5V, DHT1.VDD, RF_433_MHz_(Transmissor)1.DATA_1, R1.Pin_0

notes:
  Resistència 10K ohms Valors també vàlids:
  3.3K, 4.7K, 5.6K

custom parts:
  10K Ω Resistor: A generic 5-band resistor (0.25W)
