# Fritzing sketch esquema (saved by Fritzing 0.9.3b)
breadboards: 1

parts:
  Nano1 = Arduino Nano v2.3
  RF_433_MHz_(Receptor)1 = RF 433 MHz (Receptor)

nets:
  GND: Nano1.GND, RF_433_MHz_(Receptor)1.GND
  N1: Nano1.D11, RF_433_MHz_(Receptor)1.DATA2
  +5V: Nano1.+5V, RF_433_MHz_(Receptor)1.VCC
