# Fritzing sketch esquema (saved by Fritzing 0.9.3b)
breadboards: 1

parts:
  Nano1 = Arduino Nano v2.3
  BMP280_Breakout1 = BMP280 Breakout Board [part_number=BMP280]

nets:
  GND: Nano1.GND, BMP280_Breakout1.GND
  3V3: Nano1.3V3, BMP280_Breakout1.VCC
  N1: Nano1.A5, BMP280_Breakout1.SCL
  N2: Nano1.A4, BMP280_Breakout1.SDA

custom parts:
  BMP280 Breakout Board: This is a breakout board for the Bosch Sensortec BMP280, "an absolute barometric pressure sensor especially designed for mobile applications." The operation range is 300 to 1100 hPa. Supply voltage is 1.2 to 3.6V. Operating temperature range is -40 to +85 °C.
